// Logisim project Codigo error.circ as structural Verilog: 1 circuit, main circuit main
module main (
  input  [6:0] in_1,
  output C1,
  output [6:0] out_3,
  output C2,
  output C4
);

  wire demultiplexer_1_out1, demultiplexer_1_out2, demultiplexer_1_out3, demultiplexer_1_out4,
       demultiplexer_1_out5, demultiplexer_1_out6, demultiplexer_1_out7, xor_1_out, xor_2_out, xor_3_out,
       xor_4_out, xor_5_out, xor_6_out, xor_7_out, xor_8_out, xor_9_out;

  xor xor_1 (xor_1_out, in_1[6], in_1[4]);
  xor xor_2 (xor_2_out, in_1[5], in_1[4]);
  xor xor_3 (xor_3_out, in_1[3], in_1[2]);
  xor xor_4 (xor_4_out, xor_1_out, in_1[2]);
  xor xor_5 (xor_5_out, xor_4_out, in_1[0]);
  xor xor_6 (xor_6_out, xor_2_out, in_1[1]);
  xor xor_7 (xor_7_out, xor_6_out, in_1[0]);
  xor xor_8 (xor_8_out, xor_3_out, in_1[1]);
  xor xor_9 (xor_9_out, xor_8_out, in_1[0]);
  not not_1 (C1, xor_5_out);
  not not_2 (C2, xor_7_out);
  not not_3 (C4, xor_9_out);
  Demultiplexer #(.select(3)) demultiplexer_1 (
    .out1(demultiplexer_1_out1), .out2(demultiplexer_1_out2), .out3(demultiplexer_1_out3),
    .out4(demultiplexer_1_out4), .out5(demultiplexer_1_out5), .out6(demultiplexer_1_out6),
    .out7(demultiplexer_1_out7), .in(1'b1), .sel({C4, C2, C1}));  // open: out0, en
  xor xor_10 (out_3[6], in_1[6], demultiplexer_1_out1);
  xor xor_11 (out_3[5], in_1[5], demultiplexer_1_out2);
  xor xor_12 (out_3[4], in_1[4], demultiplexer_1_out3);
  xor xor_13 (out_3[3], in_1[3], demultiplexer_1_out4);
  xor xor_14 (out_3[2], in_1[2], demultiplexer_1_out5);
  xor xor_15 (out_3[1], in_1[1], demultiplexer_1_out6);
  xor xor_16 (out_3[0], in_1[0], demultiplexer_1_out7);
endmodule
