// Logisim project ej1.circ as structural Verilog: 1 circuit, main circuit main
module main (
  input  A,
  input  B,
  input  C,
  input  D,
  output SA,
  output SB,
  output SC,
  output SD
);

  wire and_1_out, and_2_out, and_3_out, and_4_out, and_5_out, and_6_out, and_7_out, and_8_out, and_9_out,
       and_10_out, and_11_out, and_12_out, and_13_out, and_14_out, and_15_out, and_16_out, and_17_out,
       not_1_out, not_2_out, not_3_out, not_4_out;

  not not_1 (not_1_out, A);
  not not_2 (not_2_out, B);
  not not_3 (not_3_out, C);
  not not_4 (not_4_out, D);
  and and_1 (and_1_out, not_1_out, not_2_out, C);
  and and_2 (and_2_out, not_1_out, B, not_3_out);
  and and_3 (and_3_out, A, not_2_out, not_3_out);
  and and_4 (and_4_out, A, B, C);
  and and_5 (and_5_out, not_1_out, B, not_3_out, not_4_out);
  and and_6 (and_6_out, not_1_out, not_2_out, D);
  and and_7 (and_7_out, B, C, D);
  and and_8 (and_8_out, A, not_3_out, D);
  and and_9 (and_9_out, A, not_2_out, C, not_4_out);
  and and_10 (and_10_out, not_2_out, not_3_out, D);
  and and_11 (and_11_out, not_2_out, C, not_4_out);
  and and_12 (and_12_out, A, B, not_3_out, not_4_out);
  and and_13 (and_13_out, B, C, D);
  and and_14 (and_14_out, A, not_2_out, C);
  and and_15 (and_15_out, C, D);
  and and_16 (and_16_out, B, D);
  and and_17 (and_17_out, B, C);
  or or_1 (SA, and_1_out, and_2_out, and_3_out, and_4_out);
  or or_2 (SB, and_5_out, and_6_out, and_7_out, and_8_out, and_9_out);
  or or_3 (SC, and_10_out, and_11_out, and_12_out, and_13_out, and_14_out);
  or or_4 (SD, and_15_out, and_16_out, and_17_out);
endmodule
