// Logisim project ej2.circ as structural Verilog: 1 circuit, main circuit main
module main (
  input  [3:0] \Número ,
  input  [3:0] \Número_2 ,
  input  [3:0] \Número_3 ,
  output Error,
  output Error_2,
  output out_6
);

  wire nand_1_out, nand_2_out, nand_3_out, nand_4_out, nor_1_out, nor_2_out, or_1_out;

  nor nor_1 (nor_1_out, \Número_3 [1], \Número_3 [2]);
  nor nor_2 (nor_2_out, \Número_3 [3], \Número_3 [3]);
  nand nand_1 (nand_1_out, \Número_2 [1], \Número_2 [1]);
  nand nand_2 (nand_2_out, \Número_2 [2], \Número_2 [2]);
  nor nor_3 (out_6, nor_1_out, nor_2_out);
  or or_1 (or_1_out, \Número [1], \Número [2]);
  nand nand_3 (nand_3_out, nand_1_out, nand_2_out);
  and and_1 (Error, or_1_out, \Número [3]);
  nand nand_4 (nand_4_out, nand_3_out, \Número_2 [3]);
  nand nand_5 (Error_2, nand_4_out, nand_4_out);

  // Notes on the sheet:
  //   1er APARTADO
  //   A B C D
  //   2º APARTADO
  //   A B C D
  //   A B C D
endmodule
