// Logisim project ej3.circ as structural Verilog: 2 circuits, main circuit main
module main (
  input  [3:0] CIFRA_1,
  input  [3:0] CIFRA_2,
  output ERROR
);

  wire comprobar_bcd_1_error, comprobar_bcd_2_error;

  comprobar_bcd comprobar_bcd_1 (.\Número (CIFRA_1), .Error(comprobar_bcd_1_error));
  comprobar_bcd comprobar_bcd_2 (.\Número (CIFRA_2), .Error(comprobar_bcd_2_error));
  or or_1 (ERROR, comprobar_bcd_1_error, comprobar_bcd_2_error);
endmodule

module comprobar_bcd (
  input  [3:0] \Número ,
  output Error
);

  wire or_1_out;

  or or_1 (or_1_out, \Número [1], \Número [2]);
  and and_1 (Error, or_1_out, \Número [3]);

  // Notes on the sheet:
  //   A B C D
endmodule
