// Logisim project ej4.circ as structural Verilog: 1 circuit, main circuit main
module main (
  input  [2:0] Em_S1_S2,
  output M1,
  output M2
);

  wire nor_1_out, nor_2_out, nor_3_out;

  nor nor_1 (nor_1_out, Em_S1_S2[2], Em_S1_S2[2]);
  nor nor_2 (nor_2_out, Em_S1_S2[1], Em_S1_S2[1]);
  nor nor_3 (nor_3_out, Em_S1_S2[0], Em_S1_S2[0]);
  nor nor_4 (M1, nor_1_out, nor_2_out);
  nor nor_5 (M2, nor_3_out, nor_2_out, nor_1_out);
endmodule
