// Logisim project ej5.circ as structural Verilog: 1 circuit, main circuit main
module main (
  input  [3:0] t1__t0__D__A,
  output E,
  output C
);

  wire and_1_out, not_1_out, not_2_out, not_3_out, or_1_out, or_2_out;

  not not_1 (not_1_out, t1__t0__D__A[2]);
  not not_2 (not_2_out, t1__t0__D__A[0]);
  and and_1 (and_1_out, t1__t0__D__A[1], not_2_out);
  not not_3 (not_3_out, t1__t0__D__A[3]);
  or or_1 (or_1_out, not_1_out, and_1_out);
  or or_2 (or_2_out, t1__t0__D__A[1], not_2_out);
  and and_2 (E, t1__t0__D__A[3], or_1_out);
  and and_3 (C, not_3_out, not_1_out, or_2_out);
endmodule
