// Logisim project hamming_error_simple.circ as structural Verilog: 1 circuit, main circuit main
module main (
  input  [6:0] in_1,
  output [2:0] out_2
);

  ExactlyOne xor_1 (.out(out_2[0]), .in0(in_1[6]), .in1(in_1[4]), .in2(in_1[2]), .in3(in_1[0]));
  ExactlyOne xor_2 (.out(out_2[1]), .in0(in_1[5]), .in1(in_1[4]), .in2(in_1[1]), .in3(in_1[0]));
  ExactlyOne xor_3 (.out(out_2[2]), .in0(in_1[3]), .in1(in_1[2]), .in2(in_1[1]), .in3(in_1[0]));

  // Notes on the sheet:
  //   P1,P2,M3,P4,M5,M6,M7
  //   C1
  //   C2
  //   C4
  //   Si hay algún error saldrá la posición en la que está, si no hay error saldrá 000
endmodule
