// Logisim project ej1.circ as structural Verilog: 2 circuits, main circuit main
module main (
  input  [3:0] in_1,
  input  [3:0] in_2,
  output [3:0] out_3,
  output out_4
);

  wire adder_1_cout, comprobar_bcd_1_error;
  wire [3:0] adder_1_out, adder_2_out;

  Adder #(.width(4)) adder_1 (.a(in_1), .b(in_2), .out(adder_1_out), .cout(adder_1_cout));  // open: cin
  comprobar_bcd comprobar_bcd_1 (.\Número (adder_1_out), .Error(comprobar_bcd_1_error));
  Adder #(.width(4)) adder_2 (.a(4'b0110), .b(adder_1_out), .out(adder_2_out));  // open: cin, cout
  or or_1 (out_4, comprobar_bcd_1_error, adder_1_cout);
  Multiplexer #(.width(4)) multiplexer_1 (.in0(adder_1_out), .in1(adder_2_out), .out(out_3), .sel(out_4));  // open: en

  // Notes on the sheet:
  //   Si la suma produce acarreo o el resultado es mayor que 9, habrá una decena BCD y con el multiplexor lo que hacemos es sumarle 6 si ese bit de decena está a 1, de lo contrario sale el resultado normal
endmodule

module comprobar_bcd (
  input  [3:0] \Número ,
  output Error
);

  wire or_1_out;

  or or_1 (or_1_out, \Número [1], \Número [2]);
  and and_1 (Error, or_1_out, \Número [3]);

  // Notes on the sheet:
  //   A B C D
endmodule
