// Logisim project ej3.circ as structural Verilog: 1 circuit, main circuit main
module main (
  input  C2,
  input  [3:0] in_2,
  input  [3:0] in_3,
  input  Resta,
  output [3:0] Resultado,
  output [3:0] out_6,
  output [3:0] out_7,
  output Overflow
);

  wire adder_1_cout, and_1_out, and_2_out, and_3_out, and_4_out, not_2_out, not_3_out, not_4_out, not_5_out;
  wire [3:0] multiplexer_2_out, Z;

  Multiplexer #(.width(4)) multiplexer_1 (.in0(in_3), .in1(Z), .out(out_7), .sel(Resta));  // open: en
  assign Z = ~in_3;  // NOT_Gate not_1, 4 bits wide
  Multiplexer #(.width(4)) multiplexer_2 (.in0(in_3), .in1(Z), .out(multiplexer_2_out), .sel(Resta));  // open: en
  and and_1 (and_1_out, Resta, C2);
  Adder #(.width(4)) adder_1 (.a(in_2), .b(out_7), .out(out_6), .cin(and_1_out), .cout(adder_1_cout));
  not not_2 (not_2_out, multiplexer_2_out[3]);
  not not_3 (not_3_out, Resultado[3]);
  and and_2 (and_2_out, adder_1_cout, not_4_out);
  not not_4 (not_4_out, C2);
  and and_3 (and_3_out, Resultado[3], not_2_out, not_5_out);
  not not_5 (not_5_out, in_2[3]);
  and and_4 (and_4_out, multiplexer_2_out[3], in_2[3], not_3_out);
  Adder #(.width(4)) adder_2 (.a(4'b0000), .b(out_6), .out(Resultado), .cin(and_2_out));  // open: cout
  or or_1 (Overflow, and_3_out, and_4_out);

  // Other names for the same wires on the sheet: A = Resta; B = C2; C[3:0] = in_2; D[3:0] = in_3; R[3:0] = Resultado
endmodule
