// Logisim project ej4.circ as structural Verilog: 1 circuit, main circuit main
module main (
  input  [3:0] A,
  input  [3:0] B,
  input  [3:0] C,
  output [3:0] S,
  output [1:0] N
);

  wire comparator_4_eq, comparator_5_eq, comparator_6_eq, I1, I2, I3;
  wire [1:0] or_2_out;
  wire [3:0] not_1_out, not_2_out, not_3_out, Salida_1, Salida_2, Salida_3;

  Comparator #(.width(4), .mode("unsigned")) comparator_1 (.a(Salida_1), .b(Salida_2), .eq(I1));  // open: gt, lt
  Comparator #(.width(4), .mode("unsigned")) comparator_2 (.a(Salida_2), .b(Salida_3), .eq(I2));  // open: gt, lt
  Comparator #(.width(4), .mode("unsigned")) comparator_3 (.a(Salida_1), .b(Salida_3), .eq(I3));  // open: gt, lt
  assign not_1_out = ~A;  // NOT_Gate not_1, 4 bits wide
  Comparator #(.width(4), .mode("unsigned")) comparator_4 (.a(A), .b(4'b1111), .eq(comparator_4_eq));  // open: gt, lt
  Multiplexer #(.width(4)) multiplexer_1 (.in0(A), .in1(not_1_out), .out(Salida_1), .sel(comparator_4_eq));  // open: en
  Multiplexer #(.select(2), .width(4)) multiplexer_2 (
    .in0(4'b0000), .in1(Salida_1), .in2(Salida_2), .in3(Salida_3), .out(S), .sel(or_2_out));  // open: en
  or or_1 (or_2_out[1], I1, I2);
  or or_2 (or_2_out[0], I2, I3);
  or or_3 (N[1], I1, I2, I3);
  and and_1 (N[0], I1, I3);
  assign not_2_out = ~B;  // NOT_Gate not_2, 4 bits wide
  Comparator #(.width(4), .mode("unsigned")) comparator_5 (.a(B), .b(4'b1111), .eq(comparator_5_eq));  // open: gt, lt
  Multiplexer #(.width(4)) multiplexer_3 (.in0(B), .in1(not_2_out), .out(Salida_2), .sel(comparator_5_eq));  // open: en
  assign not_3_out = ~C;  // NOT_Gate not_3, 4 bits wide
  Comparator #(.width(4), .mode("unsigned")) comparator_6 (.a(C), .b(4'b1111), .eq(comparator_6_eq));  // open: gt, lt
  Multiplexer #(.width(4)) multiplexer_4 (.in0(C), .in1(not_3_out), .out(Salida_3), .sel(comparator_6_eq));  // open: en
endmodule
