// Logisim project ej5.circ as structural Verilog: 2 circuits, main circuit main
module main (
  input  c1,
  input  [3:0] A,
  input  [3:0] B
);

  wire and_1_out, and_2_out, comparator_1_eq, comparator_2_eq, comparator_2_lt, comparator_3_eq,
       comparator_4_eq, comparator_4_gt, comparator_5_gt, comparator_6_lt, comparator_7_eq,
       multiplexer_2_out, multiplexer_3_out, or_1_out, or_2_out, SA;
  wire [2:0] MA, MB;
  wire [3:0] A_t, not_1_out, not_2_out;
  wire [3:3] Salida2;

  assign not_1_out = ~A_t;  // NOT_Gate not_1, 4 bits wide
  Comparator #(.width(4), .mode("unsigned")) comparator_1 (.a(A_t), .b(4'b1111), .eq(comparator_1_eq));  // open: gt, lt
  and and_1 (and_1_out, comparator_1_eq, c1);
  Comparator #(.width(1), .mode("unsigned")) comparator_2 (
    .a(SA), .b(Salida2[3]), .eq(comparator_2_eq), .lt(comparator_2_lt));  // open: gt
  Comparator #(.width(4), .mode("unsigned")) comparator_3 (
    .a({SA, MA}), .b({Salida2[3], MB}), .eq(comparator_3_eq));  // open: gt, lt
  Comparator #(.width(1), .mode("unsigned")) comparator_4 (
    .a(SA), .b(Salida2[3]), .gt(comparator_4_gt), .eq(comparator_4_eq));  // open: lt
  Multiplexer #(.width(4)) multiplexer_1 (.in0(A_t), .in1(not_1_out), .out({SA, MA}), .sel(and_1_out));  // open: en
  Comparator #(.width(3), .mode("unsigned")) comparator_5 (.a(MA), .b(MB), .gt(comparator_5_gt));  // open: eq, lt
  Comparator #(.width(3), .mode("unsigned")) comparator_6 (.a(MA), .b(MB), .lt(comparator_6_lt));  // open: gt, eq
  Multiplexer multiplexer_2 (
    .in0(1'b0), .in1(comparator_5_gt), .out(multiplexer_2_out), .sel(comparator_2_eq));  // open: en
  Multiplexer multiplexer_3 (
    .in0(1'b0), .in1(comparator_6_lt), .out(multiplexer_3_out), .sel(comparator_4_eq));  // open: en
  or or_1 (or_1_out, multiplexer_2_out, comparator_2_lt);
  or or_2 (or_2_out, multiplexer_3_out, comparator_4_gt);
  LED A_B (.in(or_1_out));
  LED A_B_2 (.in(comparator_3_eq));
  LED A_B_3 (.in(or_2_out));
  assign not_2_out = ~B;  // NOT_Gate not_2, 4 bits wide
  Comparator #(.width(4), .mode("unsigned")) comparator_7 (.a(B), .b(4'b1111), .eq(comparator_7_eq));  // open: gt, lt
  Multiplexer #(.width(4)) multiplexer_4 (
    .in0(B), .in1(not_2_out), .out({Salida2[3], MB}), .sel(and_2_out));  // open: en
  and and_2 (and_2_out, comparator_7_eq, c1);

  // Other names for the same wires on the sheet: Salida1[3:0] = {SA, MA}; Salida2[2:0] = MB; SB = Salida2[3]
endmodule

module c1 (
);

  wire comparator_1_eq, comparator_2_eq;
  wire [3:0] A, B, not_1_out, not_2_out, Salida1, Salida2;

  assign not_1_out = ~A;  // NOT_Gate not_1, 4 bits wide
  Comparator #(.width(4), .mode("unsigned")) comparator_1 (.a(A), .b(4'b1111), .eq(comparator_1_eq));  // open: gt, lt
  assign not_2_out = ~B;  // NOT_Gate not_2, 4 bits wide
  Comparator #(.width(4), .mode("unsigned")) comparator_2 (.a(B), .b(4'b1111), .eq(comparator_2_eq));  // open: gt, lt
  Multiplexer #(.width(4)) multiplexer_1 (.in0(A), .in1(not_1_out), .out(Salida1), .sel(comparator_1_eq));  // open: en
  Multiplexer #(.width(4)) multiplexer_2 (.in0(B), .in1(not_2_out), .out(Salida2), .sel(comparator_2_eq));  // open: en
endmodule
