// Logisim project ej6.circ as structural Verilog: 4 circuits, main circuit main
module main (
  input  in_1,
  input  in_2,
  input  in_3,
  input  in_4,
  input  in_5,
  output Aprobar_propuesta
);

  wire and_1_out, comparator_1_eq, comparator_1_gt, comparator_2_gt;
  wire [3:0] V_C_P, V_S_P;

  votos_con_peso votos_con_peso_1 (
    .Presidente(in_1), .Secretario(in_2), .Consejero_1(in_3), .Consejero_2(in_4), .Consejero_3(in_5),
    .Total_de_los_votos_con_peso(V_C_P));
  Comparator #(.width(4), .mode("unsigned")) comparator_1 (
    .a(V_C_P), .b(4'b0101), .gt(comparator_1_gt), .eq(comparator_1_eq));  // open: lt
  Comparator #(.width(4), .mode("unsigned")) comparator_2 (
    .a(V_S_P), .b(4'b0010), .gt(comparator_2_gt));  // open: eq, lt
  and and_1 (and_1_out, comparator_1_eq, comparator_2_gt);
  or or_1 (Aprobar_propuesta, comparator_1_gt, and_1_out);
  votos_sin_peso votos_sin_peso_1 (
    .Presidente(in_1), .Secretario(in_2), .Consejero_1(in_3), .Consejero_2(in_4), .Consejero_3(in_5),
    .Total_de_los_votos_sin_peso(V_S_P));

  // Other names for the same wires on the sheet: Consejero_1 = in_3; Consejero_2 = in_4; Consejero_3 = in_5;
  //   Presidente = in_1; Secretario = in_2

  // Notes on the sheet:
  //   Votos con peso
  //   Votos sin peso
endmodule

module full_adder_1_bit (
  input  A,
  input  B,
  input  Cin,
  output S1,
  output S2
);

  wire and_1_out, and_2_out, and_3_out, and_4_out, and_5_out, and_6_out, not_1_out, not_2_out, not_3_out,
       xor_1_out;

  not not_1 (not_1_out, A);
  not not_2 (not_2_out, B);
  not not_3 (not_3_out, Cin);
  xor xor_1 (xor_1_out, B, Cin);
  and and_1 (and_1_out, A, B, Cin);
  and and_2 (and_2_out, A, B);
  and and_3 (and_3_out, A, Cin);
  and and_4 (and_4_out, B, Cin);
  and and_5 (and_5_out, not_1_out, xor_1_out);
  and and_6 (and_6_out, A, not_2_out, not_3_out);
  or or_1 (S1, and_2_out, and_3_out, and_4_out);
  or or_2 (S2, and_5_out, and_1_out, and_6_out);
endmodule

module votos_con_peso (
  input  Presidente,
  input  Secretario,
  input  Consejero_1,
  input  Consejero_2,
  input  Consejero_3,
  output [3:0] Total_de_los_votos_con_peso
);

  wire full_adder_1_bit_1_s1, full_adder_1_bit_3_s2, full_adder_1_bit_4_s1, full_adder_1_bit_6_s1, LSB_secr,
       MSB_cons, MSB_pres, MSB_secr, seg_bit_pres, ter_bit_pres;

  full_adder_1_bit full_adder_1_bit_1 (.S1(full_adder_1_bit_1_s1), .S2(MSB_pres), .A(Presidente), .B(1'b0), .Cin(1'b0));
  full_adder_1_bit full_adder_1_bit_2 (.S1(MSB_secr), .S2(LSB_secr), .A(Secretario), .B(Secretario), .Cin(Secretario));
  full_adder_1_bit full_adder_1_bit_3 (
    .S1(MSB_cons), .S2(full_adder_1_bit_3_s2), .A(Consejero_1), .B(Consejero_2), .Cin(Consejero_3));
  full_adder_1_bit full_adder_1_bit_4 (
    .S1(full_adder_1_bit_4_s1), .S2(Total_de_los_votos_con_peso[0]), .A(full_adder_1_bit_1_s1), .B(LSB_secr),
    .Cin(full_adder_1_bit_3_s2));
  full_adder_1_bit full_adder_1_bit_5 (.S2(seg_bit_pres), .A(1'b0), .B(1'b0), .Cin(1'b0));  // open: S1
  full_adder_1_bit full_adder_1_bit_6 (
    .S1(full_adder_1_bit_6_s1), .S2(Total_de_los_votos_con_peso[1]), .A(full_adder_1_bit_4_s1), .B(MSB_secr),
    .Cin(MSB_cons));
  full_adder_1_bit full_adder_1_bit_7 (.S2(ter_bit_pres), .A(1'b0), .B(1'b0), .Cin(1'b0));  // open: S1
  full_adder_1_bit full_adder_1_bit_8 (
    .S1(Total_de_los_votos_con_peso[3]), .S2(Total_de_los_votos_con_peso[2]), .A(full_adder_1_bit_6_s1),
    .B(MSB_pres), .Cin(1'b0));

  // Other names for the same wires on the sheet: LSB_total = Total_de_los_votos_con_peso[0];
  //   BIT_2_total = Total_de_los_votos_con_peso[1]; BIT_3_total = Total_de_los_votos_con_peso[2];
  //   MSB_total = Total_de_los_votos_con_peso[3]

  // Notes on the sheet:
  //   ESTOS DOS SUMADORES REALMENTE SOBRAN, ES COMO PONER LOS BITS A 0 SIEMPRE
endmodule

module votos_sin_peso (
  input  Presidente,
  input  Secretario,
  input  Consejero_1,
  input  Consejero_2,
  input  Consejero_3,
  output [3:0] Total_de_los_votos_sin_peso
);

  wire full_adder_1_bit_1_s1, full_adder_1_bit_1_s2, full_adder_1_bit_2_s1, full_adder_1_bit_2_s2,
       full_adder_1_bit_3_s1;

  full_adder_1_bit full_adder_1_bit_1 (
    .S1(full_adder_1_bit_1_s1), .S2(full_adder_1_bit_1_s2), .A(Presidente), .B(Secretario), .Cin(1'b0));
  full_adder_1_bit full_adder_1_bit_2 (
    .S1(full_adder_1_bit_2_s1), .S2(full_adder_1_bit_2_s2), .A(Consejero_1), .B(Consejero_2), .Cin(1'b0));
  full_adder_1_bit full_adder_1_bit_3 (
    .S1(full_adder_1_bit_3_s1), .S2(Total_de_los_votos_sin_peso[0]), .A(full_adder_1_bit_1_s2),
    .B(full_adder_1_bit_2_s2), .Cin(Consejero_3));
  full_adder_1_bit full_adder_1_bit_4 (
    .S1(Total_de_los_votos_sin_peso[2]), .S2(Total_de_los_votos_sin_peso[1]), .A(full_adder_1_bit_1_s1),
    .B(full_adder_1_bit_3_s1), .Cin(full_adder_1_bit_2_s1));

  assign Total_de_los_votos_sin_peso[3] = 1'b0;

  // Other names for the same wires on the sheet: LSB = Total_de_los_votos_sin_peso[0];
  //   Segundo_bit = Total_de_los_votos_sin_peso[1]; MSB = Total_de_los_votos_sin_peso[2]
endmodule
