// Logisim project ej1.circ as structural Verilog: 1 circuit, main circuit main
module main (
  input  [1:0] in_1,
  output [1:0] Lata__Cambio
);

  wire and_1_out, and_2_out, and_3_out, and_4_out, and_5_out, and_6_out, and_7_out, and_8_out, and_9_out,
       and_10_out, and_11_out, clock_1_out, E0_neg, E1_neg, or_1_out, or_2_out, or_3_out, Q0, Q0_neg, Q1,
       Q1_neg, Q2_neg;

  and and_1 (and_1_out, Q1, Q0_neg, in_1[1]);
  and and_2 (and_2_out, Q0_neg, in_1[1], in_1[0]);
  and and_3 (and_3_out, Q0, E1_neg, in_1[0]);
  Clock clock_1 (.out(clock_1_out));
  D_Flip_Flop d_ff_1 (.clk(clock_1_out), .D(or_1_out), .Q(Lata__Cambio[0]), .Qn(Q2_neg));  // open: preset, en, reset
  or or_1 (or_1_out, and_1_out, and_2_out, and_3_out);
  and and_4 (and_4_out, Q1, Q0_neg, E1_neg);
  and and_5 (and_5_out, Q1_neg, in_1[1], E0_neg);
  and and_6 (and_6_out, Q0, in_1[1], E0_neg);
  and and_7 (and_7_out, Q1_neg, Q0, E1_neg, in_1[0]);
  or or_2 (or_2_out, and_4_out, and_5_out, and_6_out, and_7_out);
  D_Flip_Flop d_ff_2 (.clk(clock_1_out), .D(or_2_out), .Q(Q1), .Qn(Q1_neg));  // open: preset, en, reset
  and and_8 (and_8_out, Q1_neg, Q0, E0_neg);
  and and_9 (and_9_out, Q0_neg, E1_neg, in_1[0]);
  and and_10 (and_10_out, Q1, in_1[1], in_1[0]);
  or or_3 (or_3_out, and_8_out, and_9_out, and_10_out);
  D_Flip_Flop d_ff_3 (.clk(clock_1_out), .D(or_3_out), .Q(Q0), .Qn(Q0_neg));  // open: preset, en, reset
  and and_11 (and_11_out, Q1, Q0);
  or or_4 (Lata__Cambio[1], and_11_out, Lata__Cambio[0]);
  not not_1 (E0_neg, in_1[0]);
  not not_2 (E1_neg, in_1[1]);

  // Other names for the same wires on the sheet: E0 = in_1[0]; E1 = in_1[1]; Q2 = Lata__Cambio[0]
endmodule
