// Logisim project ej2.circ as structural Verilog: 1 circuit, main circuit main
module main (
  input  [1:0] in_1,
  output Bajar,
  output Subir
);

  wire and_1_out, and_2_out, and_3_out, and_4_out, and_5_out, and_6_out, clock_1_out, j_k_ff_1_q,
       j_k_ff_1_qn, j_k_ff_2_q, j_k_ff_2_qn, not_1_out, not_2_out, not_3_out, not_4_out;

  Clock clock_1 (.out(clock_1_out));
  not not_1 (not_1_out, in_1[1]);
  not not_2 (not_2_out, in_1[0]);
  J_K_Flip_Flop j_k_ff_1 (
    .J(in_1[1]), .clk(clock_1_out), .K(not_1_out), .Q(j_k_ff_1_q), .Qn(j_k_ff_1_qn));  // open: preset, en, reset
  J_K_Flip_Flop j_k_ff_2 (
    .J(in_1[0]), .clk(clock_1_out), .K(not_2_out), .Q(j_k_ff_2_q), .Qn(j_k_ff_2_qn));  // open: preset, en, reset
  not not_3 (not_3_out, in_1[1]);
  not not_4 (not_4_out, in_1[0]);
  and and_1 (and_1_out, j_k_ff_1_q, not_3_out);
  and and_2 (and_2_out, j_k_ff_2_q, not_3_out, not_4_out);
  and and_3 (and_3_out, j_k_ff_1_q, j_k_ff_2_q, not_4_out);
  and and_4 (and_4_out, j_k_ff_1_qn, in_1[1]);
  and and_5 (and_5_out, j_k_ff_1_qn, j_k_ff_2_qn, in_1[0]);
  and and_6 (and_6_out, j_k_ff_2_qn, in_1[1], in_1[0]);
  or or_1 (Bajar, and_1_out, and_2_out, and_3_out);
  or or_2 (Subir, and_4_out, and_5_out, and_6_out);

  // Other names for the same wires on the sheet: e0 = in_1[0]; e1 = in_1[1]
endmodule
