// Logisim project ej4.circ as structural Verilog: 1 circuit, main circuit main
module main (
  output [2:0] out_1
);

  wire and_1_out, and_2_out, CLK, Q0_NEGADO, Q1_NEGADO;

  Clock clock_1 (.out(CLK));
  J_K_Flip_Flop j_k_ff_1 (.J(1'b1), .clk(CLK), .K(1'b1), .Q(out_1[2]));  // open: Qn, preset, en, reset
  and and_1 (and_1_out, Q0_NEGADO, out_1[2]);
  J_K_Flip_Flop j_k_ff_2 (
    .J(and_1_out), .clk(CLK), .K(out_1[2]), .Q(out_1[1]), .Qn(Q1_NEGADO));  // open: preset, en, reset
  and and_2 (and_2_out, Q1_NEGADO, out_1[2]);
  J_K_Flip_Flop j_k_ff_3 (
    .J(out_1[2]), .clk(CLK), .K(and_2_out), .Q(out_1[0]), .Qn(Q0_NEGADO));  // open: preset, en, reset

  // Other names for the same wires on the sheet: Q0 = out_1[0]; Q1 = out_1[1]; Q2 = out_1[2]

  // Notes on the sheet:
  //   J2
  //   J1
  //   J0
endmodule
