// Logisim project ej_3a.circ as structural Verilog: 1 circuit, main circuit main
module main (
  input  D,
  input  C,
  input  B,
  input  A,
  input  CLR,
  input  in_6,
  input  [1:0] in_7,
  output [3:0] out_8
);

  wire multiplexer_1_out, multiplexer_2_out, multiplexer_3_out, multiplexer_4_out;

  Multiplexer #(.select(2)) multiplexer_1 (
    .in0(out_8[3]), .in1(out_8[0]), .in2(out_8[2]), .in3(D), .out(multiplexer_1_out), .sel(in_7));  // open: en
  D_Flip_Flop d_ff_1 (.clk(in_6), .D(multiplexer_1_out), .Q(out_8[3]), .reset(CLR));  // open: Qn, preset, en
  Multiplexer #(.select(2)) multiplexer_2 (
    .in0(out_8[2]), .in1(out_8[3]), .in2(out_8[1]), .in3(C), .out(multiplexer_2_out), .sel(in_7));  // open: en
  D_Flip_Flop d_ff_2 (.clk(in_6), .D(multiplexer_2_out), .Q(out_8[2]), .reset(CLR));  // open: Qn, preset, en
  Multiplexer #(.select(2)) multiplexer_3 (
    .in0(out_8[1]), .in1(out_8[2]), .in2(out_8[0]), .in3(B), .out(multiplexer_3_out), .sel(in_7));  // open: en
  D_Flip_Flop d_ff_3 (.clk(in_6), .D(multiplexer_3_out), .Q(out_8[1]), .reset(CLR));  // open: Qn, preset, en
  Multiplexer #(.select(2)) multiplexer_4 (
    .in0(out_8[0]), .in1(out_8[1]), .in2(out_8[3]), .in3(A), .out(multiplexer_4_out), .sel(in_7));  // open: en
  D_Flip_Flop d_ff_4 (.clk(in_6), .D(multiplexer_4_out), .Q(out_8[0]), .reset(CLR));  // open: Qn, preset, en

  // Other names for the same wires on the sheet: QA = out_8[0]; QB = out_8[1]; QC = out_8[2]; QD = out_8[3]; R = in_6;
  //   S1S0[1:0] = in_7
endmodule
