// Logisim project ej_3b.circ as structural Verilog: 1 circuit, main circuit main
module main (
  input  [3:0] in_1,
  output [1:0] out_2,
  output [3:0] out_3
);

  wire and_2_out, CA, CB, CC, clock_1_out, CLR, j_k_ff_1_qn, j_k_ff_2_qn, not_2_out;

  or or_1 (out_2[1], CA, CB, CC);
  not not_1 (out_2[0], CB);
  and and_1 (CLR, CB, CC, clock_1_out);
  not not_2 (not_2_out, clock_1_out);
  Clock clock_1 (.out(clock_1_out));
  J_K_Flip_Flop j_k_ff_1 (
    .J(1'b1), .clk(clock_1_out), .K(1'b1), .Q(CC), .Qn(j_k_ff_1_qn), .reset(and_2_out));  // open: preset, en
  ej_3a_main main_1 (
    .CLR(CLR), .in_7(out_2), .D(in_1[3]), .C(in_1[2]), .B(in_1[1]), .A(in_1[0]), .out_8(out_3),
    .in_6(not_2_out));
  J_K_Flip_Flop j_k_ff_2 (
    .J(1'b1), .clk(j_k_ff_1_qn), .K(1'b1), .Q(CB), .Qn(j_k_ff_2_qn), .reset(and_2_out));  // open: preset, en
  J_K_Flip_Flop j_k_ff_3 (.J(1'b1), .clk(j_k_ff_2_qn), .K(1'b1), .Q(CA), .reset(and_2_out));  // open: Qn, preset, en
  and and_2 (and_2_out, CA, CC);
endmodule
