// Logisim project ej_1_2010.circ as structural Verilog: 1 circuit, main circuit main
module main (
  input  [3:0] A,
  input  [3:0] B,
  output A_B,
  output A_B_2,
  output A_B_3
);

  wire and_1_out, and_2_out, and_3_out, and_4_out, comparator_1_gt, comparator_1_lt, multiplexer_1_out,
       multiplexer_2_out, or_1_out;

  and and_1 (and_1_out, A[3], B[3]);
  and and_2 (and_2_out, ~A[3], ~B[3]);  // AND_Gate
  or or_1 (or_1_out, and_1_out, and_2_out);
  Comparator #(.width(4), .mode("unsigned")) comparator_1 (
    .a(A), .b(B), .gt(comparator_1_gt), .lt(comparator_1_lt));  // open: eq
  Multiplexer multiplexer_1 (.in0(1'b0), .in1(comparator_1_gt), .out(multiplexer_1_out), .sel(or_1_out));  // open: en
  Multiplexer multiplexer_2 (.in0(1'b0), .in1(comparator_1_lt), .out(multiplexer_2_out), .sel(or_1_out));  // open: en
  and and_3 (and_3_out, ~A[3], B[3]);  // AND_Gate
  and and_4 (and_4_out, A[3], ~B[3]);  // AND_Gate
  or or_2 (A_B, and_3_out, multiplexer_1_out);
  or or_3 (A_B_3, multiplexer_2_out, and_4_out);
  and and_5 (A_B_2, ~A_B, ~A_B_3);  // AND_Gate
endmodule
