// Logisim project ej_2_2023.circ as structural Verilog: 1 circuit, main circuit main
module main (
  input  in_1
);

  wire and_1_out, and_2_out, and_3_out, and_4_out, and_5_out, and_6_out, clock_1_out, or_1_out, or_2_out, Q0,
       Q0n, Q1, Q1n, Q2, Q2n;

  Clock clock_1 (.out(clock_1_out));
  and and_1 (and_1_out, Q1, Q0n, ~in_1);  // AND_Gate
  D_Flip_Flop d_ff_1 (.clk(clock_1_out), .D(and_1_out), .Q(Q2), .Qn(Q2n));  // open: preset, en, reset
  and and_2 (and_2_out, Q2, in_1);
  or or_1 (or_1_out, and_2_out, and_3_out);
  LED P (.in(or_1_out));
  and and_3 (and_3_out, Q1, ~in_1, Q0);  // AND_Gate
  and and_4 (and_4_out, Q2n, in_1, Q1n);
  D_Flip_Flop d_ff_2 (.clk(clock_1_out), .D(and_4_out), .Q(Q1), .Qn(Q1n));  // open: preset, en, reset
  and and_5 (and_5_out, Q1n, Q0, in_1);
  and and_6 (and_6_out, Q2n, Q1n, Q0n, ~in_1);  // AND_Gate
  or or_2 (or_2_out, and_5_out, and_6_out);
  D_Flip_Flop d_ff_3 (.clk(clock_1_out), .D(or_2_out), .Q(Q0), .Qn(Q0n));  // open: preset, en, reset

  // Other names for the same wires on the sheet: e = in_1
endmodule
