// Logisim project ej_3_2023.circ as structural Verilog: 1 circuit, main circuit main
module main (
  output [2:0] out_1
);

  wire clock_1_out, j_k_ff_1_qn, j_k_ff_2_qn, nand_1_out, nand_2_out, not_1_out, not_2_out, not_3_out;

  Clock clock_1 (.out(clock_1_out));
  not not_1 (not_1_out, nand_1_out);
  nand nand_1 (nand_1_out, ~out_1[0], out_1[1], out_1[2]);  // NAND_Gate
  nand nand_2 (nand_2_out, out_1[0], out_1[1], ~out_1[2]);  // NAND_Gate
  J_K_Flip_Flop j_k_ff_1 (
    .J(1'b1), .clk(clock_1_out), .K(1'b1), .Q(out_1[0]), .Qn(j_k_ff_1_qn), .preset(not_1_out));  // open: en, reset
  not not_2 (not_2_out, nand_2_out);
  J_K_Flip_Flop j_k_ff_2 (
    .J(1'b1), .clk(j_k_ff_1_qn), .K(1'b1), .Q(out_1[1]), .Qn(j_k_ff_2_qn), .reset(not_2_out));  // open: preset, en
  not not_3 (not_3_out, nand_2_out);
  J_K_Flip_Flop j_k_ff_3 (
    .J(1'b1), .clk(j_k_ff_2_qn), .K(1'b1), .Q(out_1[2]), .preset(not_3_out));  // open: Qn, en, reset

  // Other names for the same wires on the sheet: Q2 = out_1[0]; Q1 = out_1[1]; Q0 = out_1[2]

  // Notes on the sheet:
  //   LSB
  //   MSB
endmodule
