// Logisim project ej_4_2025.circ as structural Verilog: 1 circuit, main circuit main
module main (
  output out_1,
  output out_2,
  output out_3
);

  wire clock_1_out, j_k_ff_1_qn, j_k_ff_2_qn, nand_1_out, not_1_out, not_2_out, not_3_out, not_4_out;

  Clock clock_1 (.out(clock_1_out));
  not not_1 (not_1_out, clock_1_out);
  nand nand_1 (nand_1_out, out_3, ~out_2, out_1);  // NAND_Gate
  J_K_Flip_Flop j_k_ff_1 (
    .J(1'b1), .clk(not_1_out), .K(1'b1), .Q(out_3), .Qn(j_k_ff_1_qn), .reset(not_2_out));  // open: preset, en
  not not_2 (not_2_out, nand_1_out);
  J_K_Flip_Flop j_k_ff_2 (
    .J(1'b1), .clk(j_k_ff_1_qn), .K(1'b1), .Q(out_2), .Qn(j_k_ff_2_qn), .reset(not_3_out));  // open: preset, en
  not not_3 (not_3_out, nand_1_out);
  J_K_Flip_Flop j_k_ff_3 (.J(1'b1), .clk(j_k_ff_2_qn), .K(1'b1), .Q(out_1), .reset(not_4_out));  // open: Qn, preset, en
  not not_4 (not_4_out, nand_1_out);
endmodule
