// Logisim project ej2_repaso_T4.circ as structural Verilog: 1 circuit, main circuit main
module main (
  input  [3:0] in_1,
  output a,
  output b
);

  wire and_1_out;

  and and_1 (and_1_out, in_1[2], ~in_1[1]);  // AND_Gate
  or or_1 (a, ~in_1[2], ~in_1[3]);  // OR_Gate
  or or_2 (b, ~in_1[3], and_1_out);  // OR_Gate
endmodule
