// Logisim project ej3_repaso_T4.circ as structural Verilog: 1 circuit, main circuit main
module main (
  input  [3:0] in_1,
  output out_2
);

  wire decoder_1_out0, decoder_1_out1, decoder_1_out2, decoder_1_out3, decoder_2_out2, decoder_2_out3,
       decoder_3_out2, decoder_3_out3, decoder_4_out0, decoder_4_out1, decoder_5_out1, decoder_5_out3;

  Decoder #(.select(2)) decoder_1 (
    .out0(decoder_1_out0), .out1(decoder_1_out1), .out2(decoder_1_out2), .out3(decoder_1_out3),
    .sel(in_1[3:2]));  // open: en
  Decoder #(.select(2)) decoder_2 (
    .out2(decoder_2_out2), .out3(decoder_2_out3), .sel(in_1[1:0]), .en(decoder_1_out0));  // open: out0, out1
  Decoder #(.select(2)) decoder_3 (
    .out2(decoder_3_out2), .out3(decoder_3_out3), .sel(in_1[1:0]), .en(decoder_1_out1));  // open: out0, out1
  Decoder #(.select(2)) decoder_4 (
    .out0(decoder_4_out0), .out1(decoder_4_out1), .sel(in_1[1:0]), .en(decoder_1_out2));  // open: out2, out3
  Decoder #(.select(2)) decoder_5 (
    .out1(decoder_5_out1), .out3(decoder_5_out3), .sel(in_1[1:0]), .en(decoder_1_out3));  // open: out0, out2
  or or_1 (out_2, decoder_2_out2, decoder_2_out3, decoder_3_out2, decoder_3_out3, decoder_4_out0, decoder_4_out1, decoder_5_out1, decoder_5_out3);

  // Other names for the same wires on the sheet: CD[1:0] = in_1[1:0]
endmodule
