// Logisim project ej4_repaso_T4.circ as structural Verilog: 1 circuit, main circuit main
module main (
  input  [3:0] A,
  input  [3:0] B,
  input  [3:0] in_3,
  output [3:0] out_4
);

  wire comparator_1_gt, comparator_2_gt;
  wire [3:0] multiplexer_1_out;

  Multiplexer #(.width(4)) multiplexer_1 (
    .in0(B), .in1(A), .out(multiplexer_1_out), .sel(comparator_1_gt));  // open: en
  Comparator #(.width(4), .mode("unsigned")) comparator_1 (.a(A), .b(B), .gt(comparator_1_gt));  // open: eq, lt
  Comparator #(.width(4), .mode("unsigned")) comparator_2 (
    .a(multiplexer_1_out), .b(in_3), .gt(comparator_2_gt));  // open: eq, lt
  Multiplexer #(.width(4)) multiplexer_2 (
    .in0(in_3), .in1(multiplexer_1_out), .out(out_4), .sel(comparator_2_gt));  // open: en

  // Other names for the same wires on the sheet: C[3:0] = in_3
endmodule
