// Logisim project ej5_repaso_T4.circ as structural Verilog: 1 circuit, main circuit main
module main (
  input  A,
  input  B,
  input  C,
  input  D,
  output out_5
);

  wire not_1_out;

  not not_1 (not_1_out, D);
  Multiplexer #(.select(3)) multiplexer_1 (
    .in0(not_1_out), .in1(not_1_out), .in2(B), .in3(not_1_out), .in4(B), .in5(D), .in6(not_1_out),
    .in7(not_1_out), .out(out_5), .sel({A, B, C}));  // open: en
endmodule
